# Fritzing sketch Paddle_of_Theseus (saved by Fritzing 0.9.3b)
breadboards: 1

parts:
  Capacitive_Touch_Sensor = Adafruit AT42QT1010 Standalone Momentary Capacitive Touch Sensor [part_number=Capacitive_Touch_Sensor]
  Microcontroller = Teensy 3.1
  6DoF_IMU = IMU Digital Combo Board 6DOF
  R5 = Resistor [tolerance=±5% resistance=1k package=THT]
  Ultrasonic_Distance_Sensor = PING Ultrasonic Sensor
  Linear_Potentiometer = SoftPot Membrane Potentiometer - 50mm [part_number=SEN-08680]
  R8 = Resistor [tolerance=±5% resistance=1k package=THT]
  R9 = Resistor [tolerance=±5% resistance=1k package=THT]
  R10 = Resistor [tolerance=±5% resistance=1k package=THT]
  RGB_LED = RGB LED (com. cathode, rbg) [package="5 mm [THT]"]
  R11 = Resistor [tolerance=±5% resistance=10k package=THT]
  RE1 = Rotary Encoder [package=THT]
  R12 = Resistor [tolerance=±5% resistance=10k package=THT]

nets:
  3V3: Capacitive_Touch_Sensor.VDD, Microcontroller.3V3, 6DoF_IMU.3.3V, Ultrasonic_Distance_Sensor.VCC, Linear_Potentiometer.leg1, R11.Pin_1, R12.Pin_1
  TEENSY_CAP_TOUCH_PIN: Capacitive_Touch_Sensor.OUT, Microcontroller.D1
  GND: Capacitive_Touch_Sensor.GND, Microcontroller.GND, 6DoF_IMU.GND, R5.Pin_1, Ultrasonic_Distance_Sensor.GND, Linear_Potentiometer.leg2, RGB_LED.common_cathode, RE1.EncoderPinC, RE1.SwitchPinE
  TEENSY_ULTRASONIC_PIN: Microcontroller.D0, Ultrasonic_Distance_Sensor.I/O
  TEENSY_ROT_ENC_CLK_PIN: Microcontroller.D3, RE1.EncoderPinA, R12.Pin_0
  TEENSY_ROT_ENC_DT_PIN: Microcontroller.D4, R11.Pin_0, RE1.EncoderPinB
  TEENSY_RGB_G_PIN: Microcontroller.D9, R10.Pin_0
  TEENSY_RGB_B_PIN: Microcontroller.D10, R9.Pin_0
  TEENSY_RGB_R_PIN: Microcontroller.D11, R8.Pin_0
  TEENSY_LIN_POT_PIN: Microcontroller.A0/D14, R5.Pin_0, Linear_Potentiometer.wiper
  TEENSY_ROT_ENC_BUTTON_PIN: Microcontroller.A2/D16, RE1.SwitchrPinD
  TEENSY_SDA_PIN: Microcontroller.A4/D18, 6DoF_IMU.SDA
  TEENSY_SCL_PIN: Microcontroller.A5/D19, 6DoF_IMU.SCL
  N1: R8.Pin_1, RGB_LED.red_anode
  N2: R9.Pin_1, RGB_LED.blue_anode
  N3: R10.Pin_1, RGB_LED.green_anode

notes:
  Paddle of Theseus, All systems of the Paddle of Theseus - NOTE: These are all breakout boards, there is NO PCB layout file, 0.1
  SpectraSymbol ThinPot
  Adafruit AT42QT1010
  SparkFun 6DoF Digital
  Parallax Ping
  YSL RGB_LED Common_Cathode
  Teensy 4.0
  Bourns PEC11L -->

custom parts:
  Adafruit AT42QT1010 Standalone Momentary Capacitive Touch Sensor: This breakout board is the simplest way to create a project with a single "momentary" capacitive touch sensor. No microcontroller is required here - just power with 1.8 to 5.5VDC and touch the pad to activate the sensor. When a capacitive load is detected (e.g. a person touches the sensor-pad area) the red LED lights up and the output pin goes high. You can also solder a wire to the middle pad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
  PING Ultrasonic Sensor: The PING)))™ ultrasonic sensor provides an easy method of distance measurement. This sensor is perfect for any number of applications that require you to perform measurements between moving or stationary objects. Interfacing to a microcontroller is a snap. A single I/O pin is used to trigger an ultrasonic burst (well above human hearing) and then "listen" for the echo return pulse. The sensor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
  SoftPot Membrane Potentiometer - 50mm: These are very thin variable potentiometers. By pressing down on various parts of the strip, the resistance linearly changes from 100Ohms to 10,000Ohms allowing the user to very accurately calculate the relative position on the strip. Can be used as an accurate positional indicator for CNC head positioning, variable user input (volume level input for example), straight user input (multiple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
  Rotary Encoder: Rotary Encoder from ALPSec11e with switch.
